# Fritzing sketch STennisBall (saved by Fritzing 0.9.3b)
circuit board: 6.84814cm x 4.81654cm
breadboards: 1

parts:
  Raspberry_Pi_4_B = Raspberry Pi 3 [part_number=RPI-3-V1.2]
  Battery-VCC = 4 x AAA Battery Mount
  MOSFET-_30N06L = Basic FET P-Channel [package="D2Pak [SMD]"]
  R1-10K = 10k Ω Resistor [package=THT]
  Diode_Rectifier_1A-50v = Rectifier Diode 1A 50V [part_number=1N4001-TP package="300 mil [THT]"]
  Solenoid = Solenoid

nets:
  N1: Raspberry_Pi_4_B.GPIO4, MOSFET-_30N06L.Gate, R1-10K.Pin_0
  N2: Raspberry_Pi_4_B.GND, Battery-VCC.-, MOSFET-_30N06L.source, R1-10K.Pin_1
  N3: Battery-VCC.+, Diode_Rectifier_1A-50v.cathode, Solenoid.pin2
  N4: MOSFET-_30N06L.drain, Diode_Rectifier_1A-50v.anode, Solenoid.pin1

custom parts:
  10k Ω Resistor: A generic resistor (0.25W)
  Rectifier Diode 1A 50V: A standard rectifier diode
